# Fritzing sketch ic880a-rpi-backplane-basic-v2 (saved by Fritzing 0.9.3b)
circuit board: 6.77cm x 6.73cm
breadboards: 1

parts:
  1 = female pin header, 20 pins [form="♀ (female)"]
  24 = female pin header, 3 pins [form="♀ (female)"]  # not connected
  21 = Generic female header - 3 pins [form="♀ (female)" package=THT]
  1_2 = Generic double row female header - 26 pins [form="♀ (female)" package=THT]
  J1 = Power Jack [package=power_jack_pth]

nets:
  N1: 1.pin13, 1_2.pin22
  N2: 1.pin14, 1_2.pin23
  N3: 1.pin15, 1_2.pin21
  N4: 1.pin16, 1_2.pin19
  N5: 1.pin17, 1_2.pin24
  N6: 21.5V, 1_2.pin2, J1.PWR

notes:
  Raspberry PI
  gnz.io
  thethingsnetwork.org

custom parts:
  Generic female header - 3 pins: Generic female header
  Generic double row female header - 26 pins: Generic double row female header
